# Fritzing sketch scheme (saved by Fritzing 0.9.3b)

parts:
  Raspberry_Pi_1 = Raspberry Pi 3 [part_number=RPI-3-V1.2]
  Часть1 = Arduino Uno (Rev3)
  X1 = USB Connectors [package=usb-a-h]  # not connected
  Часть2 = ACS712 Low Current Sensor Board v12
  Q1 = MOSFET-NCHANNEL [package=to220v]
  R1 = Resistor [tolerance=±5% resistance=220 package=THT]
  R2 = Resistor [tolerance=±5% resistance=220 package=THT]  # not connected
  R3 = Resistor [tolerance=±5% resistance=220 package=THT]  # not connected
  K1 = Relay [part_number=FRS1B-S package=THT]
  J1 = Power Jack [package=power_jack_combo]

nets:
  N1: Raspberry_Pi_1.GPIO2, Часть1.A4/SDA
  N2: Raspberry_Pi_1.GPIO3, Часть1.A5/SCL
  GND: Raspberry_Pi_1.GND, Часть1.GND, Часть2.GND, Q1.S
  N3: Часть1.A0, Часть1.D13/SCK
  N4: Часть1.A1, Часть2.VO
  N5: Часть1.D12/MISO, R1.Pin_1
  5V: Часть1.5V, Часть2.5V
  N6: Часть1.VIN, K1.COIL2
  N7: Часть2.IP+, J1.GND

notes:
  Измерение напряжения - пока с вывода контроллера
  Измерение тока
  USB modem
  Camera
  DC 5V
